# Fritzing sketch ServoTest Sketch (saved by Fritzing 0.9.10b)
breadboards: 1

parts:
  R2 = TRIMPOT [maximum_resistance=10kΩ knob_status=50% power=0.5W package=trimpot_pth_s3_lock]
  Mod1 = Amica NodeMCU DEVKIT 1.0
  Level_Shifter = 74AHCT125 [part_number=SN74AHCT125 package=dil14]
  J1 = Basic Servo
  J2 = Basic Servo
  C1 = Electrolytic Capacitor [capacitance=1000µF voltage=25V package="300 mil [THT, electrolytic]"]

nets:
  GND: R2.CCW, Mod1.pin2, Mod1.pin_9, Mod1.pin_25, Mod1.pin_29, Level_Shifter.1OE, Level_Shifter.2OE, Level_Shifter.GND, J1.gnd, J2.gnd, C1.-
  N1: R2.WIPER, Mod1.pin_16
  N2: R2.CW, Mod1.pin1, Mod1.pin_10, Mod1.pin_26
  N3: Mod1.pin_13, Level_Shifter.2A
  N4: Mod1.pin_14, Level_Shifter.1A
  VCC: Mod1.pin_30, Level_Shifter.VCC, J1.vcc, J2.vcc, C1.+
  N5: Level_Shifter.1Y, J1.pulse
  N6: Level_Shifter.2Y, J2.pulse

custom parts:
  74AHCT125: Quad Level-Shifter (3V to 5V) Quadruple Bus Buffer Gates With 3-State Outputs
